// Logisim project byteled.circ as structural Verilog: 1 circuit, main circuit main
module main (
);

  wire and_1_out, and_2_out, and_3_out, and_4_out, and_5_out, and_6_out, and_8_out, and_9_out, and_10_out,
       clock_1_out, decoder_1_out0, decoder_1_out1, decoder_1_out2, decoder_1_out3, decoder_1_out4,
       decoder_1_out5, decoder_1_out6, decoder_1_out7, decoder_1_out8, decoder_1_out9, decoder_1_out10,
       decoder_1_out11, decoder_1_out12, decoder_1_out13, decoder_1_out14, decoder_1_out15, not_1_out,
       not_2_out, xor_1_out;
  wire [2:0] bit_extender_1_out;
  wire [3:0] bitselector_1_out, multiplexer_5_out, multiplexer_21_out;
  wire [7:0] adder_1_out, adder_2_out, and_7_out, Data_dout, multiplexer_1_out, multiplexer_2_out,
       multiplexer_3_out, multiplexer_4_out, multiplexer_6_out, multiplexer_7_out, multiplexer_8_out,
       multiplexer_9_out, multiplexer_10_out, multiplexer_11_out, multiplexer_12_out, multiplexer_13_out,
       multiplexer_14_out, multiplexer_15_out, multiplexer_16_out, multiplexer_17_out, multiplexer_18_out,
       multiplexer_19_out, multiplexer_20_out, multiplexer_22_out, multiplexer_23_out, not_3_out, or_1_out,
       PC_q, r0_q, r1_q, r2_q, r3_q, r4_q, r5_q, r6_q, r7_q, r8_q, r9_q, r10_q, r11_q, r12_q, r13_q, r14_q,
       r15_q, register_1_q, register_2_q, register_3_q, register_4_q, register_5_q, register_6_q,
       register_7_q, register_8_q, shifter_1_out, shifter_2_out, subtractor_1_out, xor_2_out;
  wire [23:0] Instructions_dout;

  Clock clock_1 (.out(clock_1_out));
  RAM #(.asyncread("true"), .dataWidth(24)) Instructions (
    .addr(PC_q), .oe(1'b1), .clk(clock_1_out), .dout(Instructions_dout));  // open: we, din
  Adder adder_1 (.a(PC_q), .b(8'h1), .out(adder_1_out));  // open: cin, cout
  Register PC (.D(adder_1_out), .clk(clock_1_out), .Q(PC_q));  // open: en, clr
  not not_1 (not_1_out, Instructions_dout[23]);
  not not_2 (not_2_out, Instructions_dout[22]);
  and and_1 (and_1_out, Instructions_dout[23], not_2_out);
  and and_2 (and_2_out, and_1_out, clock_1_out);
  and and_3 (and_3_out, Instructions_dout[22], not_1_out);
  and and_4 (and_4_out, Instructions_dout[21], not_1_out);
  Register r0 (.D(multiplexer_1_out), .clk(and_2_out), .Q(r0_q));  // open: en, clr
  Register r1 (.D(multiplexer_2_out), .clk(and_2_out), .Q(r1_q));  // open: en, clr
  Register r2 (.D(multiplexer_3_out), .clk(and_2_out), .Q(r2_q));  // open: en, clr
  Register r3 (.D(multiplexer_4_out), .clk(and_2_out), .Q(r3_q));  // open: en, clr
  Multiplexer #(.width(8)) multiplexer_1 (
    .in0(r0_q), .in1(multiplexer_23_out), .out(multiplexer_1_out), .sel(decoder_1_out0));
  Multiplexer #(.width(8)) multiplexer_2 (
    .in0(r1_q), .in1(multiplexer_23_out), .out(multiplexer_2_out), .sel(decoder_1_out1));
  Multiplexer #(.width(8)) multiplexer_3 (
    .in0(r2_q), .in1(multiplexer_23_out), .out(multiplexer_3_out), .sel(decoder_1_out2));
  Multiplexer #(.width(8)) multiplexer_4 (
    .in0(r3_q), .in1(multiplexer_23_out), .out(multiplexer_4_out), .sel(decoder_1_out3));
  xor xor_1 (xor_1_out, and_3_out, and_4_out);
  Multiplexer #(.width(4)) multiplexer_5 (
    .in0(bitselector_1_out), .in1(Instructions_dout[3:0]), .out(multiplexer_5_out),
    .sel(Instructions_dout[20]));
  Multiplexer #(.select(4), .width(8)) multiplexer_6 (
    .in0(r0_q), .in1(r1_q), .in2(r2_q), .in3(r3_q), .in4(r4_q), .in5(r5_q), .in6(r6_q), .in7(r7_q),
    .in8(r8_q), .in9(r9_q), .in10(r10_q), .in11(r11_q), .in12(r12_q), .in13(r13_q), .in14(r14_q),
    .in15(r15_q), .out(multiplexer_6_out));  // open: sel
  Register r4 (.D(multiplexer_7_out), .clk(and_2_out), .Q(r4_q));  // open: en, clr
  Register r5 (.D(multiplexer_8_out), .clk(and_2_out), .Q(r5_q));  // open: en, clr
  Register r6 (.D(multiplexer_9_out), .clk(and_2_out), .Q(r6_q));  // open: en, clr
  Register r7 (.D(multiplexer_10_out), .clk(and_2_out), .Q(r7_q));  // open: en, clr
  Multiplexer #(.width(8)) multiplexer_7 (
    .in0(r4_q), .in1(multiplexer_23_out), .out(multiplexer_7_out), .sel(decoder_1_out4));
  Multiplexer #(.width(8)) multiplexer_8 (
    .in0(r5_q), .in1(multiplexer_23_out), .out(multiplexer_8_out), .sel(decoder_1_out5));
  Multiplexer #(.width(8)) multiplexer_9 (
    .in0(r6_q), .in1(multiplexer_23_out), .out(multiplexer_9_out), .sel(decoder_1_out6));
  Multiplexer #(.width(8)) multiplexer_10 (
    .in0(r7_q), .in1(multiplexer_23_out), .out(multiplexer_10_out), .sel(decoder_1_out7));
  BitSelector #(.group(4)) bitselector_1 (.in(Instructions_dout[15:8]), .out(bitselector_1_out), .sel(1'b1));
  Register r8 (.D(multiplexer_11_out), .clk(and_2_out), .Q(r8_q));  // open: en, clr
  Register r9 (.D(multiplexer_12_out), .clk(and_2_out), .Q(r9_q));  // open: en, clr
  Register r10 (.D(multiplexer_13_out), .clk(and_2_out), .Q(r10_q));  // open: en, clr
  Register r11 (.D(multiplexer_14_out), .clk(and_2_out), .Q(r11_q));  // open: en, clr
  Multiplexer #(.width(8)) multiplexer_11 (
    .in0(r8_q), .in1(multiplexer_23_out), .out(multiplexer_11_out), .sel(decoder_1_out8));
  Multiplexer #(.width(8)) multiplexer_12 (
    .in0(r9_q), .in1(multiplexer_23_out), .out(multiplexer_12_out), .sel(decoder_1_out9));
  Multiplexer #(.width(8)) multiplexer_13 (
    .in0(r10_q), .in1(multiplexer_23_out), .out(multiplexer_13_out), .sel(decoder_1_out10));
  Multiplexer #(.width(8)) multiplexer_14 (
    .in0(r11_q), .in1(multiplexer_23_out), .out(multiplexer_14_out), .sel(decoder_1_out11));
  and and_5 (and_5_out, xor_1_out, and_3_out);
  and and_6 (and_6_out, and_4_out, xor_1_out);
  Multiplexer #(.select(4), .width(8)) multiplexer_15 (
    .in0(r0_q), .in1(r1_q), .in2(r2_q), .in3(r3_q), .in4(r4_q), .in5(r5_q), .in6(r6_q), .in7(r7_q),
    .in8(r8_q), .in9(r9_q), .in10(r10_q), .in11(r11_q), .in12(r12_q), .in13(r13_q), .in14(r14_q),
    .in15(r15_q), .out(multiplexer_15_out));  // open: sel
  Register r12 (.D(multiplexer_16_out), .clk(and_2_out), .Q(r12_q));  // open: en, clr
  Register r13 (.D(multiplexer_17_out), .clk(and_2_out), .Q(r13_q));  // open: en, clr
  Register r14 (.D(multiplexer_18_out), .clk(and_2_out), .Q(r14_q));  // open: en, clr
  Register r15 (.D(multiplexer_19_out), .clk(and_2_out), .Q(r15_q), .clr(1'b1));  // open: en
  Multiplexer #(.width(8)) multiplexer_16 (
    .in0(r12_q), .in1(multiplexer_23_out), .out(multiplexer_16_out), .sel(decoder_1_out12));
  Multiplexer #(.width(8)) multiplexer_17 (
    .in0(r13_q), .in1(multiplexer_23_out), .out(multiplexer_17_out), .sel(decoder_1_out13));
  Multiplexer #(.width(8)) multiplexer_18 (
    .in0(r14_q), .in1(multiplexer_23_out), .out(multiplexer_18_out), .sel(decoder_1_out14));
  Multiplexer #(.width(8)) multiplexer_19 (
    .in0(r15_q), .in1(multiplexer_23_out), .out(multiplexer_19_out), .sel(decoder_1_out15));
  Decoder #(.enable("false"), .select(4)) decoder_1 (
    .out0(decoder_1_out0), .out1(decoder_1_out1), .out2(decoder_1_out2), .out3(decoder_1_out3),
    .out4(decoder_1_out4), .out5(decoder_1_out5), .out6(decoder_1_out6), .out7(decoder_1_out7),
    .out8(decoder_1_out8), .out9(decoder_1_out9), .out10(decoder_1_out10), .out11(decoder_1_out11),
    .out12(decoder_1_out12), .out13(decoder_1_out13), .out14(decoder_1_out14), .out15(decoder_1_out15),
    .sel(multiplexer_21_out));
  Multiplexer #(.width(8)) multiplexer_20 (
    .in0(multiplexer_15_out), .in1(Instructions_dout[15:8]), .out(multiplexer_20_out),
    .sel(Instructions_dout[19]));
  Multiplexer #(.width(4)) multiplexer_21 (
    .in0(Instructions_dout[3:0]), .in1(4'b1111), .out(multiplexer_21_out), .sel(and_8_out));
  Bit_Extender #(.out_width(3), .\type ("zero")) bit_extender_1 (.in(multiplexer_20_out), .out(bit_extender_1_out));
  Adder adder_2 (.a(multiplexer_6_out), .b(multiplexer_20_out), .out(adder_2_out));  // open: cin, cout
  Subtractor subtractor_1 (.a(multiplexer_6_out), .b(multiplexer_20_out), .out(subtractor_1_out));  // open: bin, bout
  assign or_1_out = multiplexer_6_out | multiplexer_20_out;  // OR_Gate or_1, 8 bits wide
  assign and_7_out = multiplexer_6_out & multiplexer_20_out;  // AND_Gate and_7, 8 bits wide
  Shifter shifter_1 (.in(multiplexer_6_out), .\dist (bit_extender_1_out), .out(shifter_1_out));
  Shifter #(.shift("lr")) shifter_2 (.in(multiplexer_6_out), .\dist (bit_extender_1_out), .out(shifter_2_out));
  assign xor_2_out = multiplexer_6_out ^ multiplexer_20_out;  // XOR_Gate xor_2, 8 bits wide
  assign not_3_out = ~multiplexer_6_out;  // NOT_Gate not_3, 8 bits wide
  and and_8 (and_8_out, Instructions_dout[23], Instructions_dout[22]);
  and and_9 (and_9_out, Instructions_dout[23], Instructions_dout[21]);
  Multiplexer #(.select(3), .width(8)) multiplexer_22 (
    .in0(adder_2_out), .in1(subtractor_1_out), .in2(or_1_out), .in3(and_7_out), .in4(shifter_1_out),
    .in5(shifter_2_out), .in6(xor_2_out), .in7(not_3_out), .out(multiplexer_22_out),
    .sel(Instructions_dout[18:16]));
  and and_10 (and_10_out, clock_1_out, and_5_out);
  RAM #(.asyncread("true")) Data (
    .addr(multiplexer_22_out), .we(and_8_out), .oe(and_9_out), .clk(clock_1_out), .din(multiplexer_15_out),
    .dout(Data_dout));
  Multiplexer #(.width(8)) multiplexer_23 (
    .in0(multiplexer_22_out), .in1(Data_dout), .out(multiplexer_23_out), .sel(and_9_out));
  Register register_1 (.D(r0_q), .clk(and_10_out), .Q(register_1_q), .clr(and_6_out));  // open: en
  Register register_2 (.D(r1_q), .clk(and_10_out), .Q(register_2_q), .clr(and_6_out));  // open: en
  Register register_3 (.D(r6_q), .clk(and_10_out), .Q(register_3_q), .clr(and_6_out));  // open: en
  Register register_4 (.D(r7_q), .clk(and_10_out), .Q(register_4_q), .clr(and_6_out));  // open: en
  Register register_5 (.D(r2_q), .clk(and_10_out), .Q(register_5_q), .clr(and_6_out));  // open: en
  Register register_6 (.D(r3_q), .clk(and_10_out), .Q(register_6_q), .clr(and_6_out));  // open: en
  Register register_7 (.D(r4_q), .clk(and_10_out), .Q(register_7_q), .clr(and_6_out));  // open: en
  Register register_8 (.D(r5_q), .clk(and_10_out), .Q(register_8_q), .clr(and_6_out));  // open: en
  DotMatrix #(.inputtype("row"), .matrixcols(8), .matrixrows(8)) dotmatrix_1 (
    .row0(register_1_q), .row1(register_2_q), .row2(register_5_q), .row3(register_6_q), .row4(register_7_q),
    .row5(register_8_q), .row6(register_3_q), .row7(register_4_q));

  // Notes on the sheet:
  //   Nathaniel Escaro
  //   Hrishi Mehta
  //   I pledge my honor that I have abided by the Stevens Honor System
  //   op
  //   6
  //   5
  //   Rm
  //   Rd
  //   Rn
  //   bit8
  //   Byte LED
  //   ALU
  //   Mem Write Safeguard
endmodule
